# Fritzing sketch arduino (saved by Fritzing 0.9.1b)
circuit board: 6.49111cm x 4.61366cm
breadboards: 1

parts:
  U1 = Voltage Regulator - 5V [package="TO220 [THT]"]
  Power_plug1 = Power plug
  part = Power plug  # not connected
  C4 = Ceramic Capacitor [capacitance=100nF package="200 mil [THT, multilayer]"]
  C2 = Electrolytic Capacitor [capacitance=1µF package="100 mil [THT, electrolytic]"]
  C3 = Ceramic Capacitor [capacitance=100nF package="200 mil [THT, multilayer]"]
  U2 = atmega168 [package=dip]
  R1 = Resistor [tolerance=±5% resistance=1k package=THT]
  XTAL1 = Crystal [frequency="16 Mhz" package=THT]
  S1 = Pushbutton [package="[THT]"]
  C1 = Electrolytic Capacitor [capacitance=1µF package="100 mil [THT, electrolytic]"]

nets:
  N1: U1.input_voltage, Power_plug1.VCC, C1.+
  GND: U1.GND, Power_plug1.GND, C4.0, C2.-, C3.1, U2.GND, S1.Pin_3, S1.Pin_4, C1.-
  N2: U1.output_voltage, C2.+, U2.VCC, U2.AVCC, U2.AREF, R1.Pin_0
  N3: C4.1, U2.XLAT1, XTAL1.pin_0
  N4: C3.0, U2.XLAT2, XTAL1.pin_1
  N5: U2.RESET, R1.Pin_1, S1.Pin_1, S1.Pin_2

notes:
  This is a breadboard Arduino without an FTDI chip. You can program the chip with a USB-Serial breakout board, by using an external programmer or by programming the MCU in an Arduino board and then popping it into this circuit. The power source should be at least 7 VDC. Related example: http://itp.nyu.edu/physcomp/Tutorials/ArduinoBreadboard
